# Fritzing sketch board2 (saved by Fritzing 0.9.3b)
perfboards: 1

parts:
  J1 = Screw terminal - 2 pins [package=THT]
  Q1 = Basic FET N-Channel [package="D2Pak [SMD]"]
  Q2 = Basic FET N-Channel [package="DPak [SMD]"]
  U1 = ESP32S-HiLetgo [part_number=ESP32S-HiLetgo]
  JP1 = Header 3 [package=screwterminal-3.5mm-3_lock.007s]
  JP2 = Header 3 [package=screwterminal-3.5mm-3_lock.007s]
  JP3 = Header 3 [package=screwterminal-3.5mm-3_lock.007s]
  R1 = Resistor [tolerance=±5% resistance=180 package="2010 [SMD]"]
  R2 = Resistor [tolerance=±5% resistance=10k package="1206 [SMD]"]  # not connected
  U2 = AD22100 - Voltage Output Temperature Sensor with Signal Conditioning [part_number=AD22100]
  JP4 = Header 3 [package=screwterminal-3.5mm-3_lock.007s]
  R3 = Resistor [tolerance=±5% resistance=10k package="1206 [SMD]"]  # not connected
  Q3 = PHOTOTRANSISTOR REFLECTIVE OBJECT SENSOR [package=qrb1114-side]
  L1 = Solenoid
  R4 = Resistor [tolerance=±5% resistance=1.2k package="2010 [SMD]"]
  D1 = Schottky Diode [part_number=1N5817 package="300 mil [THT]"]
  Power_plug1 = Power plug
  R5 = Resistor [tolerance=±5% resistance=1.2k package="0402 [SMD]"]
  U3 = RELAY-SOLIDSTATE [package=relay-s108t02]
  U4 = POT [package=pot_alpha_rv16af-20]

nets:
  N1: J1.pin1, U1.GPIO8
  N2: J1.pin2, U1.GPIO6, Power_plug1.GND
  N3: Q1.Gate, R4.Pin_0
  N4: Q1.drain, L1.pin1, D1.anode
  N5: Q2.Gate, R5.Pin_0
  N6: Q2.drain, U3.T1
  N7: U1.GND, U4.S
  N8: U1.GPIO2, R4.Pin_1
  N9: U1.GPIO0, R5.Pin_1
  N10: U1.GPIO4, JP4.3
  N11: U1.GPIO23, JP3.3
  N12: JP1.2, U4.A
  N13: JP2.2, U4.E
  N14: JP3.1, R1.Pin_1
  N15: JP3.2, Q3.E, Q3.K
  N16: U2.V+, JP4.2
  N17: L1.pin2, D1.cathode, Power_plug1.VCC, U3.T2

custom parts:
  ESP32S-HiLetgo: HiLetgo ESP-WROOM-32 ESP32 ESP-32S Development Board 2.4GHz Dual-Mode WiFi + Bluetooth Dual Cores Microcontroller The ESP32 integrated with Antenna switches, RF Balun, power amplifiers, low-noise amplifiers, filters, and management modules, and the entire solution occupies the least area of PCB. 2.4 GHz Wi-Fi plus Bluetooth dual-mode chip, with TSMC Ultra-low power consumption 40nm technology,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
