# Fritzing sketch control_board (saved by Fritzing 0.9.3b)
circuit board: 11.6681cm x 7.48023cm
breadboards: 1

parts:
  R1 = Resistor [tolerance=±5% resistance=220 package=THT]
  U1 = ESP32S-HiLetgo [part_number=ESP32S-HiLetgo]
  R2 = Trimmer Potentiometer [maximum_resistance=10kΩ package=THT]
  3_3v = Pad [width=7.902222222222222 height=9.0311111111111106 connect=center]
  Ground = Pad [width=7.902222222222222 height=9.0311111111111106 connect=center]
  5v = Pad [width=7.902222222222222 height=9.0311111111111106 connect=center]
  LCD1 = LCD screen
  Q1 = PNP-Transistor [package="TO92 [THT]"]

nets:
  N1: R1.Pin_0, Q1.B
  N2: R1.Pin_1, U1.GPIO13
  N3: U1.3.3, R2.leg1, 3_3v.pad
  N4: U1.GPIO36, R2.wiper
  VIN: U1.VIN, 5v.pad, LCD1.VDD
  N5: U1.GPIO21, LCD1.LED-
  N6: U1.GPIO22, LCD1.LED+
  N7: R2.leg2, Ground.pad, LCD1.VSS, Q1.E

custom parts:
  ESP32S-HiLetgo: HiLetgo ESP-WROOM-32 ESP32 ESP-32S Development Board 2.4GHz Dual-Mode WiFi + Bluetooth Dual Cores Microcontroller The ESP32 integrated with Antenna switches, RF Balun, power amplifiers, low-noise amplifiers, filters, and management modules, and the entire solution occupies the least area of PCB. 2.4 GHz Wi-Fi plus Bluetooth dual-mode chip, with TSMC Ultra-low power consumption 40nm technology,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
